// Logisim project 12.Triggers_Registers.4.Counters.circ as structural Verilog: 1 circuit, main circuit main
module main (
  input  in_1,
  input  in_2,
  input  in_3,
  input  in_4,
  input  [3:0] in_5,
  output [3:0] out_6,
  output [3:0] out_7,
  output [3:0] out_8,
  output [3:0] out_9,
  output [3:0] out_10,
  output [3:0] out_11,
  output [3:0] out_12
);

  wire d_ff_1_qn, d_ff_2_qn, d_ff_3_qn, d_ff_4_qn;

  T_Flip_Flop t_ff_1 (.clk(in_1), .T(in_1), .Q(out_6[1]));  // open: Qn, preset, reset
  D_Flip_Flop #(.trigger("falling")) d_ff_1 (
    .clk(in_2), .D(d_ff_1_qn), .Q(out_7[0]), .Qn(d_ff_1_qn));  // open: preset, reset
  Counter #(.max('hf), .width(4)) counter_1 (.Q(out_8), .clk(in_3));  // open: load, D, count, carry, up, clr
  Counter #(.max('hf), .width(4)) counter_2 (.Q(out_10), .clk(in_4));  // open: load, D, count, carry, up, clr
  T_Flip_Flop t_ff_2 (.clk(out_6[1]), .T(out_6[1]), .Q(out_6[2]));  // open: Qn, preset, reset
  D_Flip_Flop #(.trigger("falling")) d_ff_2 (
    .clk(out_7[0]), .D(d_ff_2_qn), .Q(out_7[1]), .Qn(d_ff_2_qn));  // open: preset, reset
  T_Flip_Flop t_ff_3 (.clk(out_6[2]), .T(out_6[2]), .Q(out_6[3]));  // open: Qn, preset, reset
  D_Flip_Flop #(.trigger("falling")) d_ff_3 (
    .clk(out_7[1]), .D(d_ff_3_qn), .Q(out_7[2]), .Qn(d_ff_3_qn));  // open: preset, reset
  not not_1 (out_9[0], out_8[0]);
  not not_2 (out_9[1], out_8[1]);
  not not_3 (out_9[2], out_8[2]);
  not not_4 (out_9[3], out_8[3]);
  assign out_11 = ~out_10;  // NOT_Gate not_5, 4 bits wide
  T_Flip_Flop t_ff_4 (.clk(out_6[3]), .T(out_6[3]));  // open: Q, Qn, preset, reset
  D_Flip_Flop #(.trigger("falling")) d_ff_4 (
    .clk(out_7[2]), .D(d_ff_4_qn), .Q(out_7[3]), .Qn(d_ff_4_qn));  // open: preset, reset
  Adder #(.width(4)) adder_1 (.a(out_11), .b(in_5), .out(out_12));  // open: cin, cout

  assign out_6[0] = in_1;

  // Notes on the sheet:
  //   1. Уменьшающий счётчик по фротну
  //   2. Увеличивающий счётчик по спаду
  //   3. Увеличивающий и уменьшающий
  //   4. С заданным начальным значением
endmodule
