// Logisim project 13.Triggers_Registers.1.RS.circ as structural Verilog: 1 circuit, main circuit main
module main (
  input  R,
  input  S,
  input  in_3,
  output Q,
  output nQ,
  output Q_2,
  output nQ_2
);

  nor nor_1 (Q, R, nQ);
  nor nor_2 (nQ, Q, S);
  nor nor_3 (Q_2, in_3, nQ_2);
  nor nor_4 (nQ_2, Q_2, in_3);

  // Notes on the sheet:
  //   1. RS-триггер -- наше всё
  //   2. Некорректное состояние RS
endmodule
